// Logisim project ALU.circ as structural Verilog: 1 circuit, main circuit ALU
module ALU (
  input  [31:0] OperandA,
  input  [31:0] Result,
  input  [31:0] OperandB,
  input  [3:0] Operation
);

  wire clock_1_out, comparator_1_lt, comparator_2_lt, undriven;
  wire [31:0] ADD, AND, NOR, OR, RND, SLT, SLTU, SUB, XOR;

  Adder #(.width(32)) adder_1 (.a(OperandA), .b(OperandB), .out(ADD));  // open: cin, cout
  Subtractor #(.width(32)) subtractor_1 (.a(OperandA), .b(OperandB), .out(SUB));  // open: bin, bout
  Multiplexer #(.select(4), .width(32)) multiplexer_1 (
    .in0(ADD), .in1(SUB), .in2(AND), .in3(OR), .in4(NOR), .in5(XOR), .in6(SLT), .in7(SLTU), .in8(RND),
    .out(Result), .sel(Operation), .en(undriven));  // open: in9, in10, in11, in12, in13, in14, in15
  assign OR = OperandA | OperandB;  // OR_Gate or_1, 32 bits wide
  // Probe on OperandA
  // Probe on Result
  assign AND = OperandA & OperandB;  // AND_Gate and_1, 32 bits wide
  assign NOR = ~(OperandA | OperandB);  // NOR_Gate nor_1, 32 bits wide
  assign XOR = OperandA ^ OperandB;  // XOR_Gate xor_1, 32 bits wide
  // Probe on OperandB
  // Probe on Operation
  Comparator #(.width(32)) comparator_1 (.a(OperandA), .b(OperandB), .lt(comparator_1_lt));  // open: gt, eq
  Comparator #(.width(32), .mode("unsigned")) comparator_2 (
    .a(OperandA), .b(OperandB), .lt(comparator_2_lt));  // open: gt, eq
  assign SLT = {{31{1'b0}}, comparator_1_lt};  // Bit_Extender bit_extender_1
  assign SLTU = {{31{1'b0}}, comparator_2_lt};  // Bit_Extender bit_extender_2
  Clock clock_1 (.out(clock_1_out));
  Random #(.width(32)) random_1 (.clk(clock_1_out), .next(1'b1), .out(RND));  // open: clr

  // Other names for the same wires on the sheet: A[31:0] = OperandA; B[31:0] = OperandB; OP[3:0] = Operation

  // Notes on the sheet:
  //   INPUTS
  //   ARITHMETIC INSTRUCTIONS
  //   mulu,mult,divu,div, addi?
  //   OUTPUTS
  //   LOGIC INSTRUCTIONS
  //   andi,ori,xori?
  //   VISUALIZE INPUTS/OUTPUTS 
  //   COMPARISON INSTRUCTIONS
  //   sltiu?
  //   Falling edge?
  //   SPECIAL INSTRUCTIONS
endmodule
